# Fritzing sketch carrito (saved by Fritzing 0.9.0b)
breadboards: 1

parts:
  IC1 = H-Bridge [package=THT]
  M1 = DC Motor
  M2 = DC Motor
  Parte1 = Arduino Mega 2560 (Rev3)
  Parte2 = SRF05 Ultrasonic Rangefinder

nets:
  N1: IC1.1A, Parte1.D4_PWM
  N2: IC1.1Y, M2.pin_2
  GND: IC1.GND1, IC1.GND2, IC1.GND3, IC1.GND4, Parte1.GND, Parte2.GND
  N3: IC1.2Y, M2.pin_1
  N4: IC1.2A, Parte1.D5_PWM
  5V: IC1.VCC2, IC1.VCC1, Parte1.5V, Parte2.VCC
  N5: IC1.3A, Parte1.D3_PWM
  N6: IC1.3Y, M1.pin_2
  N7: IC1.4Y, M1.pin_1
  N8: IC1.4A, Parte1.D2_PWM
  N9: Parte1.D9_PWM, Parte2.Trig
  N10: Parte1.D8_PWM, Parte2.Echo
